// Digital circuit mp5i.dig as structural Verilog
module mp5i (
  input  clk,
  output [7:0] display,
  output [15:0] mirout
);

  wire _4_bit_clock_delay_1_p2, _4_bit_clock_delay_1_p3, _4_bit_clock_delay_1_p4, _4_bit_clock_delay_1_p5,
       or_1_out;
  wire [4:0] mp4_min_1_p6, MPC_q, multiplexer_1_out;
  wire [7:0] mp4_min_1_p4, mp4_min_1_p5, rom_1_d;
  wire [7:5] mp4_min_1_p6_2;
  wire [15:0] Microprogram_Store_d;

  ROM #(.AddrBits(8), .Bits(8)) rom_1 (.A(mp4_min_1_p4), .sel(or_1_out), .D(rom_1_d));
  // _4_bit_clock_delay _4_bit_clock_delay_1: pin names not known; wires that end beside it: clk, _4_bit_clock_delay_1_p2, _4_bit_clock_delay_1_p3, _4_bit_clock_delay_1_p4, _4_bit_clock_delay_1_p5
  or or_1 (or_1_out, _4_bit_clock_delay_1_p3, _4_bit_clock_delay_1_p4);
  Multiplexer #(.Bits(5)) multiplexer_1 (
    .sel(mirout[10]), .in_0(mirout[15:11]), .in_1(mp4_min_1_p6), .out(multiplexer_1_out));
  Register #(.Bits(5), .isProgramCounter("true")) MPC (
    .D(multiplexer_1_out), .C(_4_bit_clock_delay_1_p5), .en(_4_bit_clock_delay_1_p5), .Q(MPC_q));
  EEPROM #(.AddrBits(5), .isProgramMemory("true"), .Bits(16)) Microprogram_Store (
    .A(MPC_q), .CS(1'b1), .WE(1'b0), .OE(1'b1), .D(Microprogram_Store_d));
  // mp4_min mp4_min_1: pin names not known; wires that end beside it: display, mirout[6:2], _4_bit_clock_delay_1_p4, mp4_min_1_p4, mp4_min_1_p5, {mp4_min_1_p6_2, mp4_min_1_p6}, mirout[1:0], mirout[9:7]
  Register #(.Bits(8)) register_1 (
    .D(rom_1_d), .C(_4_bit_clock_delay_1_p4), .en(_4_bit_clock_delay_1_p4), .Q(mp4_min_1_p5));
  Register #(.Bits(16)) MIR (
    .D(Microprogram_Store_d), .C(_4_bit_clock_delay_1_p2), .en(_4_bit_clock_delay_1_p2), .Q(mirout));

  // Notes on the sheet:
  //   clk: Hz: 5
  //   contents of rom_1 (hex, n*v repeats v):
  //   8,8,e,b,b,17,11
  //   Microprogram_Store loads MP5-microcode.hex
endmodule
